# Fritzing sketch MIDI-AmpChannelSwitcher (saved by Fritzing 0.9.3b)
breadboards: 1

parts:
  Part1 = Adafruit Metro Mini [part_number="Adafruit #2590"]
  JACK1 = 2.1mm Barrel Jack with Terminal Block
  TRS1 = Audio Jack (TRS) 3.5mm [package="4Ucon 08780 [THT]"]
  R1 = Resistor [tolerance=±5% resistance=220 package=THT]
  D1 = Diode [package=diode-1n4148]
  IC1 = IC, DIP package, 8 pins [chip_label=6N138]
  R2 = Resistor [tolerance=±5% resistance=10k package=THT]
  R3 = Resistor [tolerance=±5% resistance=470 package=THT]
  R4 = Resistor [tolerance=±5% resistance=680 package=THT]
  LED2 = LED - 3mm [color="Red (633nm)" package="3 mm [THT]"]
  R5 = Resistor [tolerance=±5% resistance=220 package=THT]
  LED3 = LED - 3mm [color="Red (633nm)" package="3 mm [THT]"]
  IC2 = IC, DIP package, 10 pins [chip_label=TQ2L-5V]
  IC3 = IC, DIP package, 10 pins [chip_label=TQ2L-5V]
  TRS2 = Audio Jack (TRS) 3.5mm [package="4Ucon 08780 [THT]"]

nets:
  N1: Part1.IO11, IC3.pin10
  N2: Part1.IO10, IC3.pin1
  N3: Part1.IO9, IC2.pin10
  N4: Part1.IO8, IC2.pin1
  N5: Part1.IO6, R5.Pin_0
  N6: Part1.IO5, R4.Pin_0
  N7: Part1.IO2, IC1.pin6, R3.Pin_1
  N8: Part1.+5V, IC1.pin8, R3.Pin_0
  N9: Part1.GND, JACK1.NEG, IC1.pin5, R2.Pin_0, LED2.cathode, LED3.cathode
  N10: Part1.VIN, JACK1.POS
  N11: TRS1.Ring, D1.C, IC1.pin2
  N12: TRS1.Tip, R1.Pin_0
  N13: R1.Pin_1, D1.A, IC1.pin3
  N14: IC1.pin7, R2.Pin_1
  N15: R4.Pin_1, LED2.anode
  N16: R5.Pin_1, LED3.anode
  N17: IC2.pin7, IC3.pin7, TRS2.Sleeve
  N18: IC2.pin8, TRS2.Tip
  N19: IC3.pin8, TRS2.Ring

notes:
  RING - MIDI 4 (Green)
  TIP - MIDI 5 (Blue)
  DIODE is 1N4148
  PIN 1 ON 6N138 has Circle
  1/4" TRS to Amp Footswitch
  TIP = Yellow
  RING = White
  SLEEVE = Black
  Pinout for TQ2-L-5V Relay

custom parts:
  Adafruit Metro Mini: We sure love the ATmega328 here at Adafruit, and we use them a lot for our own projects. The processor has plenty of GPIO, Analog inputs, hardware UART SPI and I2C, timers and PWM galore - just enough for most simple projects. When we need to go small, we use a Pro Trinket 3V or 5V, but if you want to have USB-to-Serial built in, we reach for an Adafruit METRO Mini. METRO Mini is the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
